# Fritzing sketch 555 Snow Globe (saved by Fritzing 0.9.8b)
breadboards: 1

parts:
  U1 = 555 Timer [package="SO8 [SMD]"]  # not connected
  BATT1 = 4xAA Switchable Battery Pack w/Bare Wire
  C1 = Electrolytic Capacitor [capacitance=1µF voltage=16V package="100 mil [THT, electrolytic]"]
  R1 = Resistor [tolerance=±5% power=0.25 resistance=4.7k package=THT]  # not connected

nets:
  N1: BATT1.NEG, C1.-

custom parts:
  4xAA Switchable Battery Pack w/Bare Wire: 4xAA Switchable Battery Pack with Bare Wire connection
